# Fritzing sketch Lasertag (saved by Fritzing 0.9.2b)
breadboards: 1

parts:
  Part1 = Arduino Uno (Rev3)
  R1 = Photocell (LDR) [package=THT]
  R2 = Photocell (LDR) [package=THT]
  R3 = Photocell (LDR) [package=THT]
  R4 = Resistor [tolerance=±5% resistance=220 package=THT]
  R5 = Resistor [tolerance=±5% resistance=220 package=THT]
  R6 = Resistor [tolerance=±5% resistance=220 package=THT]
  LED1 = LED - 5mm [color="Red (633nm)" package="5 mm [THT]"]
  LED2 = LED - 5mm [color="Red (633nm)" package="5 mm [THT]"]
  LED3 = LED - 5mm [color="Red (633nm)" package="5 mm [THT]"]
  R7 = Resistor [tolerance=±5% resistance=220 package=THT]
  R8 = Resistor [tolerance=±5% resistance=220 package=THT]
  R9 = Resistor [tolerance=±5% resistance=220 package=THT]
  J1 = Piezo Speaker

nets:
  N1: Part1.A0, R3.pin_0
  N2: Part1.A1, R2.pin_0, R5.Pin_1
  N3: Part1.A2, R1.pin_0, R4.Pin_1
  N4: Part1.D2, LED3.anode
  N5: Part1.D3_PWM, LED2.anode
  N6: Part1.D4, LED1.anode
  N7: Part1.D7, J1.pin2
  N8: Part1.5V, R1.pin_1, R2.pin_1, R3.pin_1
  N9: Part1.GND, R4.Pin_0, R5.Pin_0, R6.Pin_0, R7.Pin_1, R8.Pin_1, R9.Pin_1
  N10: LED1.cathode, R7.Pin_0
  N11: LED2.cathode, R8.Pin_0
  N12: LED3.cathode, R9.Pin_0
